// Logisim project week_1_dld_Ali_Irfan.circ as structural Verilog
module Q1 (
  input  A,
  input  B,
  input  C,
  output X
);

  wire and_1_out, and_2_out, and_3_out, and_4_out, and_5_out, and_6_out, and_7_out, and_8_out, and_9_out,
       and_10_out, not_1_out, not_2_out, not_3_out, not_4_out, not_5_out, not_6_out, not_7_out, not_8_out,
       not_9_out, or_1_out, or_2_out, or_3_out;

  not not_1 (not_1_out, B);
  not not_2 (not_2_out, A);
  and and_1 (and_1_out, A, not_1_out);
  and and_2 (and_2_out, not_2_out, B);
  not not_3 (not_3_out, A);
  not not_4 (not_4_out, B);
  not not_5 (not_5_out, A);
  not not_6 (not_6_out, B);
  not not_7 (not_7_out, B);
  and and_3 (and_3_out, and_1_out, C);
  and and_4 (and_4_out, and_2_out, C);
  and and_5 (and_5_out, not_3_out, not_4_out);
  and and_6 (and_6_out, not_5_out, not_6_out);
  not not_8 (not_8_out, C);
  and and_7 (and_7_out, A, not_7_out);
  not not_9 (not_9_out, C);
  or or_1 (or_1_out, and_3_out, and_4_out);
  or or_2 (or_2_out, or_1_out, and_8_out);
  and and_8 (and_8_out, and_5_out, C);
  and and_9 (and_9_out, and_6_out, not_8_out);
  or or_3 (or_3_out, and_9_out, and_10_out);
  and and_10 (and_10_out, and_7_out, not_9_out);
  or or_4 (X, or_2_out, or_3_out);
endmodule

module Q2 (
  input  x,
  input  y,
  input  z,
  output F
);

  wire and_1_out, and_2_out, not_1_out, not_2_out;

  not not_1 (not_1_out, y);
  not not_2 (not_2_out, x);
  and and_1 (and_1_out, not_1_out, z);
  and and_2 (and_2_out, not_2_out, y);
  or or_1 (F, and_1_out, and_2_out);
endmodule

module Q3 (
  input  A,
  input  B,
  input  C,
  output F
);

  wire and_1_out, and_2_out, and_3_out, not_1_out, not_2_out, not_3_out, not_4_out, not_5_out, not_6_out,
       or_1_out, or_2_out, or_3_out, or_4_out, or_5_out, or_6_out, or_7_out, or_8_out, or_9_out, or_10_out;

  or or_1 (or_1_out, A, B);
  or or_2 (or_2_out, or_1_out, C);
  or or_3 (or_3_out, A, B);
  or or_4 (or_4_out, or_3_out, not_1_out);
  not not_1 (not_1_out, C);
  or or_5 (or_5_out, A, not_2_out);
  not not_2 (not_2_out, B);
  or or_6 (or_6_out, A, not_3_out);
  not not_3 (not_3_out, B);
  not not_4 (not_4_out, C);
  not not_5 (not_5_out, A);
  or or_7 (or_7_out, not_5_out, not_6_out);
  not not_6 (not_6_out, B);
  and and_1 (and_1_out, or_2_out, or_4_out);
  or or_8 (or_8_out, or_5_out, C);
  or or_9 (or_9_out, or_6_out, not_4_out);
  or or_10 (or_10_out, or_7_out, C);
  and and_2 (and_2_out, and_1_out, or_8_out);
  and and_3 (and_3_out, or_9_out, or_10_out);
  and and_4 (F, and_2_out, and_3_out);
endmodule

module Q4 (
  input  A,
  input  B,
  input  C,
  input  D,
  output F
);

  wire and_1_out, and_2_out, and_3_out, and_4_out, and_5_out, and_6_out, and_7_out, and_8_out, and_9_out,
       and_10_out, and_11_out, and_12_out, and_13_out, and_14_out, and_15_out, and_16_out, and_17_out,
       and_18_out, and_19_out, and_20_out, and_21_out, and_22_out, and_23_out, and_24_out, and_25_out,
       and_26_out, not_1_out, not_2_out, not_3_out, not_4_out, not_5_out, not_6_out, not_7_out, not_8_out,
       not_9_out, not_10_out, not_11_out, not_12_out, not_13_out, not_14_out, not_15_out, not_16_out,
       not_17_out, not_18_out, not_19_out, or_1_out, or_2_out, or_3_out, or_4_out, or_5_out, or_6_out,
       or_7_out;

  not not_1 (not_1_out, B);
  and and_1 (and_1_out, not_1_out, not_2_out);
  not not_2 (not_2_out, C);
  not not_3 (not_3_out, D);
  not not_4 (not_4_out, A);
  and and_2 (and_2_out, not_4_out, B);
  not not_5 (not_5_out, C);
  and and_3 (and_3_out, not_5_out, not_6_out);
  not not_6 (not_6_out, D);
  not not_7 (not_7_out, C);
  not not_8 (not_8_out, D);
  not not_9 (not_9_out, A);
  not not_10 (not_10_out, B);
  not not_11 (not_11_out, B);
  not not_12 (not_12_out, A);
  not not_13 (not_13_out, B);
  not not_14 (not_14_out, D);
  not not_15 (not_15_out, A);
  not not_16 (not_16_out, D);
  not not_17 (not_17_out, D);
  not not_18 (not_18_out, B);
  not not_19 (not_19_out, D);
  and and_4 (and_4_out, and_1_out, not_3_out);
  and and_5 (and_5_out, and_2_out, and_3_out);
  and and_6 (and_6_out, A, B);
  and and_7 (and_7_out, not_7_out, not_8_out);
  and and_8 (and_8_out, not_9_out, not_10_out);
  and and_9 (and_9_out, C, D);
  and and_10 (and_10_out, A, not_11_out);
  and and_11 (and_11_out, C, D);
  and and_12 (and_12_out, not_12_out, not_13_out);
  and and_13 (and_13_out, C, not_14_out);
  and and_14 (and_14_out, not_15_out, B);
  and and_15 (and_15_out, C, not_16_out);
  and and_16 (and_16_out, A, B);
  and and_17 (and_17_out, C, not_17_out);
  and and_18 (and_18_out, A, not_18_out);
  and and_19 (and_19_out, C, not_19_out);
  or or_1 (or_1_out, and_4_out, and_5_out);
  and and_20 (and_20_out, and_6_out, and_7_out);
  and and_21 (and_21_out, and_8_out, and_9_out);
  and and_22 (and_22_out, and_10_out, and_11_out);
  and and_23 (and_23_out, and_12_out, and_13_out);
  and and_24 (and_24_out, and_14_out, and_15_out);
  and and_25 (and_25_out, and_16_out, and_17_out);
  and and_26 (and_26_out, and_18_out, and_19_out);
  or or_2 (or_2_out, or_1_out, and_20_out);
  or or_3 (or_3_out, and_21_out, and_22_out);
  or or_4 (or_4_out, and_23_out, and_24_out);
  or or_5 (or_5_out, and_25_out, and_26_out);
  or or_6 (or_6_out, or_2_out, or_3_out);
  or or_7 (or_7_out, or_4_out, or_5_out);
  or or_8 (F, or_6_out, or_7_out);
endmodule

module Q5 (
  input  W,
  input  X,
  input  Y,
  input  Z,
  output F
);

  wire and_1_out, not_1_out, not_2_out, or_1_out;

  not not_1 (not_1_out, W);
  not not_2 (not_2_out, X);
  and and_1 (and_1_out, not_1_out, not_2_out);
  or or_1 (or_1_out, and_1_out, Z);
  or or_2 (F, or_1_out, Y);
endmodule

module Q6 (
  input  A,
  input  B,
  input  C,
  input  D,
  input  E,
  output F
);

  wire and_1_out, and_2_out, and_3_out, and_4_out, and_5_out, and_6_out, and_7_out, and_8_out, and_9_out,
       and_10_out, and_11_out, and_12_out, and_13_out, and_14_out, and_15_out, and_16_out, and_17_out,
       and_18_out, and_19_out, and_20_out, and_21_out, and_22_out, and_23_out, and_24_out, and_25_out,
       and_26_out, and_27_out, and_28_out, and_29_out, and_30_out, and_31_out, not_1_out, not_2_out,
       not_3_out, not_4_out, not_5_out, not_6_out, not_7_out, not_8_out, not_9_out, not_10_out, not_11_out,
       not_12_out, not_13_out, not_14_out, not_15_out, not_16_out, not_17_out, not_18_out, not_19_out,
       not_20_out, not_21_out, or_1_out, or_2_out, or_3_out, or_4_out, or_5_out, or_6_out, or_7_out;

  not not_1 (not_1_out, B);
  not not_2 (not_2_out, C);
  not not_3 (not_3_out, C);
  not not_4 (not_4_out, E);
  not not_5 (not_5_out, A);
  not not_6 (not_6_out, A);
  not not_7 (not_7_out, B);
  not not_8 (not_8_out, B);
  and and_1 (and_1_out, not_1_out, not_2_out);
  and and_2 (and_2_out, D, E);
  and and_3 (and_3_out, B, not_3_out);
  and and_4 (and_4_out, D, not_4_out);
  not not_9 (not_9_out, A);
  not not_10 (not_10_out, E);
  not not_11 (not_11_out, A);
  not not_12 (not_12_out, B);
  and and_5 (and_5_out, not_5_out, B);
  not not_13 (not_13_out, D);
  and and_6 (and_6_out, not_6_out, not_7_out);
  not not_14 (not_14_out, C);
  not not_15 (not_15_out, D);
  not not_16 (not_16_out, E);
  not not_17 (not_17_out, C);
  and and_7 (and_7_out, A, not_8_out);
  not not_18 (not_18_out, C);
  and and_8 (and_8_out, A, B);
  not not_19 (not_19_out, C);
  not not_20 (not_20_out, D);
  not not_21 (not_21_out, E);
  and and_9 (and_9_out, and_1_out, and_2_out);
  or or_1 (or_1_out, and_9_out, and_10_out);
  and and_10 (and_10_out, and_3_out, and_4_out);
  and and_11 (and_11_out, not_9_out, B);
  and and_12 (and_12_out, and_11_out, and_13_out);
  and and_13 (and_13_out, D, not_10_out);
  and and_14 (and_14_out, not_11_out, not_12_out);
  and and_15 (and_15_out, and_14_out, and_16_out);
  and and_16 (and_16_out, D, E);
  and and_17 (and_17_out, and_5_out, C);
  and and_18 (and_18_out, and_17_out, and_19_out);
  and and_19 (and_19_out, not_13_out, E);
  and and_20 (and_20_out, and_6_out, not_14_out);
  and and_21 (and_21_out, and_20_out, and_22_out);
  and and_22 (and_22_out, not_15_out, not_16_out);
  and and_23 (and_23_out, A, B);
  and and_24 (and_24_out, and_23_out, and_25_out);
  and and_25 (and_25_out, not_17_out, D);
  and and_26 (and_26_out, and_7_out, not_18_out);
  and and_27 (and_27_out, and_26_out, and_28_out);
  and and_28 (and_28_out, D, E);
  and and_29 (and_29_out, and_8_out, not_19_out);
  and and_30 (and_30_out, and_29_out, and_31_out);
  and and_31 (and_31_out, not_20_out, not_21_out);
  or or_2 (or_2_out, or_1_out, and_12_out);
  or or_3 (or_3_out, and_15_out, and_18_out);
  or or_4 (or_4_out, and_21_out, and_24_out);
  or or_5 (or_5_out, and_27_out, and_30_out);
  or or_6 (or_6_out, or_2_out, or_3_out);
  or or_7 (or_7_out, or_4_out, or_5_out);
  or or_8 (F, or_6_out, or_7_out);
endmodule
