// Logisim project week_2_DLD_Ali_Irfan.circ as structural Verilog: 13 circuits, main circuit Half Adder
module Half_Adder (
  input  A,
  input  B,
  output C,
  output S
);

  and and_1 (C, A, B);
  xor xor_1 (S, A, B);
endmodule

module Full_Adder_using_Basic_Gates (
  input  A,
  input  B,
  input  Cin,
  output S,
  output C
);

  wire and_1_out, and_2_out, and_3_out, xor_1_out;

  xor xor_1 (xor_1_out, A, B);
  and and_1 (and_1_out, A, B);
  and and_2 (and_2_out, A, Cin);
  and and_3 (and_3_out, B, Cin);
  xor xor_2 (S, xor_1_out, Cin);
  or or_1 (C, and_1_out, and_2_out, and_3_out);

  // Notes on the sheet:
  //   Using Basic Gates
endmodule

module Full_Adder_2_Half (
  input  A,
  input  B,
  input  Cin,
  output C,
  output S
);

  wire half_adder_1_c, half_adder_1_s, half_adder_2_c;

  Half_Adder half_adder_1 (.C(half_adder_1_c), .A(A), .S(half_adder_1_s), .B(B));
  Half_Adder half_adder_2 (.C(half_adder_2_c), .A(Cin), .S(S), .B(half_adder_1_s));
  or or_1 (C, half_adder_1_c, half_adder_2_c);

  // Notes on the sheet:
  //   Using Two Half Adders
endmodule

module Full_Adder (
  input  A,
  input  B,
  input  C,
  output SUM,
  output CARRY
);

  wire and_1_out, and_2_out, and_3_out, xor_1_out;

  xor xor_1 (xor_1_out, A, B);
  and and_1 (and_1_out, A, B);
  and and_2 (and_2_out, B, C);
  and and_3 (and_3_out, A, C);
  xor xor_2 (SUM, xor_1_out, C);
  or or_1 (CARRY, and_1_out, and_2_out, and_3_out);
endmodule

module _4_BIT_RIPPLE_CARRY_ADDER (
  input  A3,
  input  A2,
  input  A1,
  input  A0,
  input  B3,
  input  B2,
  input  B1,
  input  B0,
  input  in_9,
  output Cout,
  output S,
  output S_2,
  output S_3,
  output S_4
);

  wire full_adder_using_basics_2_c, full_adder_using_basics_3_c, full_adder_using_basics_4_c;

  Full_Adder_using_Basic_Gates full_adder_using_basics_1 (
    .A(A3), .B(B3), .Cin(full_adder_using_basics_2_c), .S(S), .C(Cout));
  Full_Adder_using_Basic_Gates full_adder_using_basics_2 (
    .A(B2), .B(A2), .Cin(full_adder_using_basics_3_c), .S(S_2), .C(full_adder_using_basics_2_c));
  Full_Adder_using_Basic_Gates full_adder_using_basics_3 (
    .A(A1), .B(B1), .Cin(full_adder_using_basics_4_c), .S(S_3), .C(full_adder_using_basics_3_c));
  Full_Adder_using_Basic_Gates full_adder_using_basics_4 (
    .A(A0), .B(B0), .Cin(in_9), .S(S_4), .C(full_adder_using_basics_4_c));
endmodule

module Half_Subtracor (
  input  a,
  input  b,
  output difference,
  output borrow
);

  wire and_1_out, and_2_out, not_1_out, not_2_out, not_3_out;

  not not_1 (not_1_out, a);
  not not_2 (not_2_out, b);
  not not_3 (not_3_out, a);
  and and_1 (and_1_out, not_1_out, b);
  and and_2 (and_2_out, a, not_2_out);
  and and_3 (borrow, not_3_out, b);
  or or_1 (difference, and_1_out, and_2_out);
endmodule

module Full_Subtractor (
  input  A,
  input  B,
  input  Bin_Borrow_In,
  output Difference,
  output Borrow_Out
);

  wire adder_1_cout, not_1_out;

  not not_1 (not_1_out, Bin_Borrow_In);
  Adder #(.width(1)) adder_1 (.a(B), .b(not_1_out), .out(Difference), .cin(A), .cout(adder_1_cout));
  not not_2 (Borrow_Out, adder_1_cout);
endmodule

module ALU (
  input  A,
  input  B,
  input  [1:0] SEL,
  input  EN,
  output out_5
);

  wire adder_1_out, and_1_out, or_1_out, subtractor_1_out;

  or or_1 (or_1_out, A, B);
  and and_1 (and_1_out, A, B);
  Adder #(.width(1)) adder_1 (.a(A), .b(B), .out(adder_1_out), .cin(1'b1));  // open: cout
  Subtractor #(.width(1)) subtractor_1 (.a(A), .b(B), .out(subtractor_1_out), .bin(1'b1));  // open: bout
  Multiplexer #(.select(2)) multiplexer_1 (
    .in0(or_1_out), .in1(and_1_out), .in2(adder_1_out), .in3(subtractor_1_out), .out(out_5), .sel(SEL),
    .en(EN));
endmodule

module BCD_to_7_SEGMENT (
  input  w,
  input  x,
  input  y,
  input  z
);

  wire and_1_out, and_2_out, and_3_out, and_4_out, and_5_out, and_6_out, and_7_out, and_8_out, and_9_out,
       and_10_out, and_11_out, and_12_out, and_13_out, and_14_out, and_15_out, and_16_out, not_1_out,
       not_2_out, not_3_out, not_4_out, not_5_out, not_6_out, not_7_out, not_8_out, not_9_out, not_10_out,
       not_11_out, not_12_out, not_13_out, not_14_out, not_15_out, not_16_out, not_17_out, not_18_out,
       not_19_out, not_20_out, not_21_out, or_1_out, or_2_out, or_3_out, or_4_out, or_5_out, or_6_out,
       or_7_out;

  not not_1 (not_1_out, x);
  not not_2 (not_2_out, z);
  not not_3 (not_3_out, y);
  not not_4 (not_4_out, z);
  not not_5 (not_5_out, y);
  not not_6 (not_6_out, x);
  not not_7 (not_7_out, z);
  not not_8 (not_8_out, x);
  not not_9 (not_9_out, z);
  not not_10 (not_10_out, y);
  not not_11 (not_11_out, x);
  not not_12 (not_12_out, z);
  not not_13 (not_13_out, z);
  not not_14 (not_14_out, y);
  not not_15 (not_15_out, z);
  not not_16 (not_16_out, y);
  not not_17 (not_17_out, z);
  not not_18 (not_18_out, x);
  not not_19 (not_19_out, y);
  not not_20 (not_20_out, z);
  and and_1 (and_1_out, not_1_out, not_2_out);
  and and_2 (and_2_out, x, z);
  not not_21 (not_21_out, x);
  and and_3 (and_3_out, not_3_out, not_4_out);
  or or_1 (or_1_out, not_21_out, and_3_out, and_4_out);
  and and_4 (and_4_out, y, z);
  or or_2 (or_2_out, not_5_out, z, x);
  and and_5 (and_5_out, not_6_out, not_7_out);
  and and_6 (and_6_out, not_8_out, y);
  and and_7 (and_7_out, y, not_9_out);
  and and_8 (and_8_out, x, not_10_out, z);
  and and_9 (and_9_out, not_11_out, not_12_out);
  or or_3 (or_3_out, and_9_out, and_10_out);
  and and_10 (and_10_out, y, not_13_out);
  and and_11 (and_11_out, not_14_out, not_15_out);
  and and_12 (and_12_out, x, not_16_out);
  and and_13 (and_13_out, x, not_17_out);
  and and_14 (and_14_out, not_18_out, y);
  and and_15 (and_15_out, x, not_19_out);
  and and_16 (and_16_out, x, not_20_out);
  or or_4 (or_4_out, and_1_out, y, and_2_out, w);
  or or_5 (or_5_out, and_5_out, and_6_out, and_7_out, and_8_out, w);
  or or_6 (or_6_out, and_11_out, and_12_out, and_13_out, w);
  or or_7 (or_7_out, and_14_out, and_15_out, and_16_out, w);
  _7_Segment_Display u_7_segment_display_1 (
    .g(or_7_out), .f(or_6_out), .a(or_4_out), .b(or_1_out), .e(or_3_out), .d(or_5_out), .c(or_2_out));  // open: dp
endmodule

module CHALLENGE_ACTIVITY_1 (
  input  p2,
  input  p3,
  input  p1,
  input  p2_2,
  input  p3_2,
  output Y,
  output Z
);

  wire and_1_out, and_2_out, not_1_out, not_2_out;

  not not_1 (not_1_out, p3);
  not not_2 (not_2_out, p2_2);
  and and_1 (and_1_out, p2, not_1_out);
  and and_2 (and_2_out, p1, not_2_out);
  or or_1 (Y, and_1_out, p3);
  or or_2 (Z, and_2_out, p3_2);

  // Notes on the sheet:
  //   Control priority level of printing jobs
endmodule

module CHALLENGE_ACTIVITY_2 (
  input  S1,
  input  S2,
  input  S3,
  input  S1_2,
  input  S2_2,
  input  S3_2,
  input  S1_3,
  input  S2_3,
  input  S3_3,
  output ARM_1,
  output ARM_2,
  output ARM_3
);

  wire not_1_out, not_2_out, not_3_out;

  not not_1 (not_1_out, S3);
  not not_2 (not_2_out, S2_3);
  not not_3 (not_3_out, S3_3);
  and and_1 (ARM_1, S1, S2, not_1_out);
  and and_2 (ARM_2, S1_2, S2_2, S3_2);
  and and_3 (ARM_3, S1_3, not_2_out, not_3_out);

  // Notes on the sheet:
  //   Process line control problem
endmodule

module CHALLENGE_ACTIVITY_3 (
  input  a,
  input  b,
  input  c,
  input  d,
  output LESS,
  output EQUAL,
  output GREATER
);

  wire and_1_out, and_2_out, and_3_out, and_4_out, and_5_out, and_6_out, and_7_out, and_8_out, and_9_out,
       and_10_out, and_11_out, and_12_out, and_13_out, and_14_out, and_15_out, and_16_out, and_17_out,
       and_18_out, and_19_out, and_20_out, and_21_out, and_22_out, not_1_out, not_2_out, not_3_out,
       not_4_out, not_5_out, not_6_out, not_7_out, not_8_out, not_9_out, not_10_out, not_11_out, not_12_out,
       not_13_out, not_14_out, not_15_out, not_16_out, or_1_out, or_2_out, or_3_out, or_4_out;

  not not_1 (not_1_out, a);
  not not_2 (not_2_out, b);
  not not_3 (not_3_out, a);
  not not_4 (not_4_out, b);
  not not_5 (not_5_out, c);
  not not_6 (not_6_out, d);
  not not_7 (not_7_out, a);
  not not_8 (not_8_out, c);
  not not_9 (not_9_out, b);
  not not_10 (not_10_out, d);
  not not_11 (not_11_out, c);
  and and_1 (and_1_out, not_1_out, not_2_out);
  and and_2 (and_2_out, and_1_out, d);
  not not_12 (not_12_out, a);
  and and_3 (and_3_out, not_12_out, c);
  not not_13 (not_13_out, b);
  and and_4 (and_4_out, not_13_out, c);
  and and_5 (and_5_out, not_3_out, not_4_out);
  and and_6 (and_6_out, and_5_out, and_7_out);
  and and_7 (and_7_out, not_5_out, not_6_out);
  and and_8 (and_8_out, not_7_out, b);
  and and_9 (and_9_out, and_8_out, and_10_out);
  and and_10 (and_10_out, not_8_out, d);
  and and_11 (and_11_out, a, not_9_out);
  and and_12 (and_12_out, and_11_out, and_13_out);
  and and_13 (and_13_out, c, not_10_out);
  and and_14 (and_14_out, a, b);
  and and_15 (and_15_out, and_14_out, and_16_out);
  and and_16 (and_16_out, c, d);
  and and_17 (and_17_out, b, not_11_out);
  and and_18 (and_18_out, and_17_out, not_14_out);
  not not_14 (not_14_out, d);
  and and_19 (and_19_out, a, not_15_out);
  not not_15 (not_15_out, c);
  and and_20 (and_20_out, a, b);
  not not_16 (not_16_out, d);
  or or_1 (or_1_out, and_2_out, and_3_out);
  and and_21 (and_21_out, and_4_out, d);
  or or_2 (or_2_out, and_6_out, and_9_out);
  or or_3 (or_3_out, and_12_out, and_15_out);
  or or_4 (or_4_out, and_18_out, and_19_out);
  and and_22 (and_22_out, and_20_out, not_16_out);
  or or_5 (LESS, or_1_out, and_21_out);
  or or_6 (EQUAL, or_2_out, or_3_out);
  or or_7 (GREATER, or_4_out, and_22_out);

  // Notes on the sheet:
  //   Comparison Problem AB AND CD
endmodule

module CHALLENGE_ACTIVITY_4 (
  input  IGNITION,
  input  ENGINE_TEMP_S2,
  input  in_3,
  input  IGNITION_2,
  input  ENGINE_TEMP_S2_2,
  input  ENGINE_OIL__S3,
  output ENGINE,
  output FA,
  output OA
);

  wire and_1_out, and_2_out, not_1_out, not_2_out, not_3_out, not_4_out, not_5_out, not_6_out;

  not not_1 (not_1_out, ENGINE_TEMP_S2);
  not not_2 (not_2_out, in_3);
  not not_3 (not_3_out, ENGINE_TEMP_S2_2);
  not not_4 (not_4_out, ENGINE_OIL__S3);
  not not_5 (not_5_out, IGNITION_2);
  and and_1 (and_1_out, IGNITION, not_1_out, not_2_out);
  not not_6 (not_6_out, IGNITION);
  and and_2 (and_2_out, not_6_out, not_1_out, in_3);
  and and_3 (FA, IGNITION_2, not_3_out, not_4_out);
  and and_4 (OA, not_5_out, ENGINE_TEMP_S2_2, ENGINE_OIL__S3);
  or or_1 (ENGINE, and_1_out, and_2_out);

  // Notes on the sheet:
  //   ENGINE OIL (S3)
  //   CAR PROBLEM
endmodule
