// Logisim project WEEK3_DLD_ALI_IRFAN.circ as structural Verilog: 20 circuits, main circuit 3 bit grey code J-K flip flop counter
module MOD_10_counter (
  input  in_1,
  input  in_2,
  output Q3,
  output Q2,
  output Q1,
  output Q0,
  output out_7
);

  wire and_1_out, and_2_out, and_3_out, and_4_out, and_5_out, and_6_out, and_7_out, and_8_out, and_9_out,
       and_10_out, and_11_out, d_ff_1_qn, d_ff_2_qn, d_ff_3_qn, d_ff_4_qn, or_1_out, or_2_out, or_3_out,
       or_4_out;

  and and_1 (and_1_out, d_ff_4_qn, d_ff_2_qn, d_ff_1_qn);
  and and_2 (and_2_out, d_ff_4_qn, Q1, d_ff_1_qn);
  and and_3 (and_3_out, d_ff_3_qn, d_ff_2_qn, d_ff_1_qn);
  and and_4 (and_4_out, d_ff_4_qn, d_ff_2_qn, Q0);
  and and_5 (and_5_out, d_ff_4_qn, Q1, d_ff_1_qn);
  and and_6 (and_6_out, d_ff_3_qn, d_ff_2_qn, Q0);
  and and_7 (and_7_out, d_ff_4_qn, Q2, d_ff_2_qn);
  and and_8 (and_8_out, d_ff_4_qn, Q2, d_ff_1_qn);
  and and_9 (and_9_out, d_ff_4_qn, d_ff_3_qn, Q1, Q0);
  and and_10 (and_10_out, Q3, d_ff_3_qn, d_ff_2_qn);
  and and_11 (and_11_out, d_ff_4_qn, Q2, Q1, Q0);
  or or_1 (or_1_out, and_10_out, and_11_out);
  or or_2 (or_2_out, and_1_out, and_2_out, and_3_out);
  or or_3 (or_3_out, and_4_out, and_5_out, and_6_out);
  or or_4 (or_4_out, and_7_out, and_8_out, and_9_out);
  D_Flip_Flop d_ff_1 (.clk(in_2), .D(or_2_out), .Q(Q0), .Qn(d_ff_1_qn), .en(in_1), .reset(out_7));  // open: preset
  D_Flip_Flop d_ff_2 (.clk(in_2), .D(or_3_out), .Q(Q1), .Qn(d_ff_2_qn), .en(in_1), .reset(out_7));  // open: preset
  D_Flip_Flop d_ff_3 (.clk(in_2), .D(or_4_out), .Q(Q2), .Qn(d_ff_3_qn), .en(in_1), .reset(out_7));  // open: preset
  D_Flip_Flop d_ff_4 (.clk(in_2), .D(or_1_out), .Q(Q3), .Qn(d_ff_4_qn), .en(in_1), .reset(out_7));  // open: preset
  and and_12 (out_7, Q3, Q1);
endmodule

module MOD_6_counter (
  input  in_1,
  input  in_2,
  output Q3,
  output Q2,
  output Q1,
  output Q0,
  output out_7
);

  wire and_1_out, and_2_out, and_3_out, and_4_out, and_5_out, and_6_out, and_7_out, and_8_out, and_9_out,
       and_10_out, and_11_out, d_ff_1_qn, d_ff_2_qn, d_ff_3_qn, d_ff_4_qn, or_1_out, or_2_out, or_3_out,
       or_4_out;

  and and_1 (and_1_out, d_ff_4_qn, d_ff_2_qn, d_ff_1_qn);
  and and_2 (and_2_out, d_ff_4_qn, Q1, d_ff_1_qn);
  and and_3 (and_3_out, d_ff_3_qn, d_ff_2_qn, d_ff_1_qn);
  and and_4 (and_4_out, d_ff_4_qn, d_ff_2_qn, Q0);
  and and_5 (and_5_out, d_ff_4_qn, Q1, d_ff_1_qn);
  and and_6 (and_6_out, d_ff_3_qn, d_ff_2_qn, Q0);
  and and_7 (and_7_out, d_ff_4_qn, Q2, d_ff_2_qn);
  and and_8 (and_8_out, d_ff_4_qn, Q2, d_ff_1_qn);
  and and_9 (and_9_out, d_ff_4_qn, d_ff_3_qn, Q1, Q0);
  and and_10 (and_10_out, Q3, d_ff_3_qn, d_ff_2_qn);
  and and_11 (and_11_out, d_ff_4_qn, Q2, Q1, Q0);
  or or_1 (or_1_out, and_10_out, and_11_out);
  or or_2 (or_2_out, and_1_out, and_2_out, and_3_out);
  or or_3 (or_3_out, and_4_out, and_5_out, and_6_out);
  or or_4 (or_4_out, and_7_out, and_8_out, and_9_out);
  D_Flip_Flop d_ff_1 (.clk(in_2), .D(or_2_out), .Q(Q0), .Qn(d_ff_1_qn), .en(in_1), .reset(out_7));  // open: preset
  D_Flip_Flop d_ff_2 (.clk(in_2), .D(or_3_out), .Q(Q1), .Qn(d_ff_2_qn), .en(in_1), .reset(out_7));  // open: preset
  D_Flip_Flop d_ff_3 (.clk(in_2), .D(or_4_out), .Q(Q2), .Qn(d_ff_3_qn), .en(in_1), .reset(out_7));  // open: preset
  D_Flip_Flop d_ff_4 (.clk(in_2), .D(or_1_out), .Q(Q3), .Qn(d_ff_4_qn), .en(in_1), .reset(out_7));  // open: preset
  and and_12 (out_7, Q2, Q1);
endmodule

module _3_bit_grey_code_J_K_flip_flop_counter (
  output out_1,
  output out_2,
  output out_3
);

  wire and_1_out, and_2_out, and_3_out, and_4_out, and_5_out, and_6_out, and_7_out, and_8_out, clock_1_out,
       j_k_ff_1_qn, j_k_ff_2_qn, j_k_ff_3_qn, or_1_out, or_2_out;

  and and_1 (and_1_out, j_k_ff_3_qn, out_2);
  and and_2 (and_2_out, j_k_ff_2_qn, j_k_ff_3_qn);
  Clock clock_1 (.out(clock_1_out));
  J_K_Flip_Flop j_k_ff_1 (
    .J(and_1_out), .clk(clock_1_out), .K(and_2_out), .Q(out_1), .Qn(j_k_ff_1_qn));  // open: preset, en, reset
  and and_3 (and_3_out, j_k_ff_1_qn, out_3);
  and and_4 (and_4_out, out_1, out_3);
  J_K_Flip_Flop j_k_ff_2 (
    .J(and_3_out), .clk(clock_1_out), .K(and_4_out), .Q(out_2), .Qn(j_k_ff_2_qn));  // open: preset, en, reset
  and and_5 (and_5_out, j_k_ff_1_qn, j_k_ff_2_qn);
  and and_6 (and_6_out, out_2, out_1);
  and and_7 (and_7_out, j_k_ff_1_qn, out_2);
  and and_8 (and_8_out, out_1, j_k_ff_2_qn);
  or or_1 (or_1_out, and_5_out, and_6_out);
  or or_2 (or_2_out, and_7_out, and_8_out);
  J_K_Flip_Flop j_k_ff_3 (
    .J(or_1_out), .clk(clock_1_out), .K(or_2_out), .Q(out_3), .Qn(j_k_ff_3_qn));  // open: preset, en, reset
endmodule

module _3_bit_grey_code_D_flip_flop_counter (
  output out_1,
  output out_2,
  output out_3
);

  wire and_1_out, and_2_out, and_3_out, and_4_out, and_5_out, and_6_out, clock_1_out, d_ff_1_qn, d_ff_2_qn,
       d_ff_3_qn, or_1_out, or_2_out, or_3_out;

  and and_1 (and_1_out, out_2, d_ff_3_qn);
  and and_2 (and_2_out, out_1, out_3);
  Clock clock_1 (.out(clock_1_out));
  or or_1 (or_1_out, and_1_out, and_2_out);
  and and_3 (and_3_out, d_ff_3_qn, out_2);
  and and_4 (and_4_out, d_ff_1_qn, out_3);
  D_Flip_Flop d_ff_1 (.clk(clock_1_out), .D(or_1_out), .Q(out_1), .Qn(d_ff_1_qn));  // open: preset, en, reset
  or or_2 (or_2_out, and_3_out, and_4_out);
  D_Flip_Flop d_ff_2 (.clk(clock_1_out), .D(or_2_out), .Q(out_2), .Qn(d_ff_2_qn));  // open: preset, en, reset
  and and_5 (and_5_out, d_ff_1_qn, d_ff_2_qn);
  and and_6 (and_6_out, out_1, out_2);
  or or_3 (or_3_out, and_5_out, and_6_out);
  D_Flip_Flop d_ff_3 (.clk(clock_1_out), .D(or_3_out), .Q(out_3), .Qn(d_ff_3_qn));  // open: preset, en, reset
endmodule

module Ex__MEALY_STATE_MACHINE (
  input  in_1,
  output Q2,
  output Q1,
  output Q0
);

  wire and_1_out, and_2_out, and_3_out, and_4_out, and_5_out, and_6_out, and_7_out, and_8_out, and_9_out,
       clock_1_out, d_ff_1_qn, d_ff_2_qn, d_ff_3_qn, not_1_out, or_1_out, or_2_out, or_3_out;

  not not_1 (not_1_out, in_1);
  and and_1 (and_1_out, d_ff_1_qn, d_ff_2_qn, d_ff_3_qn);
  and and_2 (and_2_out, d_ff_2_qn, d_ff_1_qn, in_1);
  and and_3 (and_3_out, Q2, Q1, Q0, in_1);
  and and_4 (and_4_out, d_ff_3_qn, d_ff_1_qn, not_1_out);
  and and_5 (and_5_out, d_ff_3_qn, d_ff_2_qn, Q0, in_1);
  and and_6 (and_6_out, Q2, Q1, Q0, in_1);
  and and_7 (and_7_out, d_ff_2_qn, d_ff_1_qn, not_1_out);
  and and_8 (and_8_out, Q2, Q1, Q0, in_1);
  and and_9 (and_9_out, d_ff_3_qn, Q1, d_ff_1_qn, in_1);
  or or_1 (or_1_out, and_1_out, and_2_out, and_3_out);
  or or_2 (or_2_out, and_4_out, and_5_out, and_6_out);
  or or_3 (or_3_out, and_7_out, and_8_out, and_9_out);
  Clock clock_1 (.out(clock_1_out));
  D_Flip_Flop d_ff_1 (.clk(clock_1_out), .D(or_1_out), .Q(Q0), .Qn(d_ff_1_qn));  // open: preset, en, reset
  D_Flip_Flop d_ff_2 (.clk(clock_1_out), .D(or_2_out), .Q(Q1), .Qn(d_ff_2_qn));  // open: preset, en, reset
  D_Flip_Flop d_ff_3 (.clk(clock_1_out), .D(or_3_out), .Q(Q2), .Qn(d_ff_3_qn));  // open: preset, en, reset
endmodule

module _4_bit_counter_using_JK (
  input  in_1,
  output out_2,
  output out_3,
  output out_4,
  output out_5
);

  wire clock_1_out, j_k_ff_1_q, j_k_ff_2_q, j_k_ff_3_q;

  Clock clock_1 (.out(clock_1_out));
  J_K_Flip_Flop j_k_ff_1 (
    .J(in_1), .clk(clock_1_out), .K(in_1), .Q(j_k_ff_1_q), .Qn(out_5), .en(in_1));  // open: preset, reset
  J_K_Flip_Flop j_k_ff_2 (
    .J(in_1), .clk(j_k_ff_1_q), .K(in_1), .Q(j_k_ff_2_q), .Qn(out_4), .en(in_1));  // open: preset, reset
  J_K_Flip_Flop j_k_ff_3 (
    .J(in_1), .clk(j_k_ff_2_q), .K(in_1), .Q(j_k_ff_3_q), .Qn(out_3), .en(in_1));  // open: preset, reset
  J_K_Flip_Flop j_k_ff_4 (.J(in_1), .clk(j_k_ff_3_q), .K(in_1), .Qn(out_2), .en(in_1));  // open: Q, preset, reset
endmodule

module JK_FlipFlop_3_Bit_Counter (
  output Q2,
  output Q1,
  output Q0
);

  wire and_1_out, and_2_out, and_3_out, and_4_out, and_5_out, and_6_out, clock_1_out, FF0_qn, FF2_qn,
       or_1_out;

  and and_1 (and_1_out, FF2_qn, FF0_qn);
  and and_2 (and_2_out, Q2, Q0);
  and and_3 (and_3_out, Q1, Q0);
  and and_4 (and_4_out, FF2_qn, Q1);
  and and_5 (and_5_out, Q2, Q1, Q0);
  or or_1 (or_1_out, and_1_out, and_2_out);
  and and_6 (and_6_out, Q1, Q0);
  Clock clock_1 (.out(clock_1_out));
  J_K_Flip_Flop FF0 (.J(and_4_out), .clk(clock_1_out), .K(and_5_out), .Q(Q0), .Qn(FF0_qn));  // open: preset, en, reset
  J_K_Flip_Flop FF1 (.J(or_1_out), .clk(clock_1_out), .K(and_3_out), .Q(Q1));  // open: Qn, preset, en, reset
  J_K_Flip_Flop FF2 (.J(and_6_out), .clk(clock_1_out), .K(and_6_out), .Q(Q2), .Qn(FF2_qn));  // open: preset, en, reset
endmodule

module D_FlipFlop_3_Bit_Counter (
  output Q2,
  output Q1,
  output Q0
);

  wire and_1_out, and_2_out, and_3_out, and_4_out, and_5_out, and_6_out, clock_1_out, d_ff_1_qn, d_ff_2_qn,
       d_ff_3_qn, or_1_out, or_2_out, or_3_out;

  and and_1 (and_1_out, Q1, d_ff_3_qn);
  and and_2 (and_2_out, Q2, d_ff_2_qn, Q0);
  and and_3 (and_3_out, d_ff_3_qn, d_ff_1_qn);
  and and_4 (and_4_out, Q2, d_ff_2_qn, Q0);
  and and_5 (and_5_out, d_ff_3_qn, Q1, Q0);
  and and_6 (and_6_out, Q2, d_ff_2_qn, Q0);
  Clock clock_1 (.out(clock_1_out));
  or or_1 (or_1_out, and_1_out, and_2_out);
  or or_2 (or_2_out, and_3_out, and_4_out);
  or or_3 (or_3_out, and_5_out, and_6_out);
  D_Flip_Flop d_ff_1 (.clk(clock_1_out), .D(or_1_out), .Q(Q0), .Qn(d_ff_1_qn));  // open: preset, en, reset
  D_Flip_Flop d_ff_2 (.clk(clock_1_out), .D(or_2_out), .Q(Q1), .Qn(d_ff_2_qn));  // open: preset, en, reset
  D_Flip_Flop d_ff_3 (.clk(clock_1_out), .D(or_3_out), .Q(Q2), .Qn(d_ff_3_qn));  // open: preset, en, reset
endmodule

module States (
  input  S1,
  input  S2,
  input  S3,
  output A3,
  output A2,
  output A1
);

  wire not_1_out, not_2_out;

  not not_1 (not_1_out, S2);
  not not_2 (not_2_out, S3);
  and and_1 (A3, S1, not_1_out);
  and and_2 (A2, S2, not_2_out);

  assign A1 = S3;
endmodule

module SISO_Register (
  input  in_1,
  output out_2
);

  wire clock_1_out, d_ff_1_q, d_ff_2_q, d_ff_3_q;

  Clock clock_1 (.out(clock_1_out));
  D_Flip_Flop d_ff_1 (.clk(clock_1_out), .D(in_1), .Q(d_ff_1_q));  // open: Qn, preset, en, reset
  D_Flip_Flop d_ff_2 (.clk(clock_1_out), .D(d_ff_1_q), .Q(d_ff_2_q));  // open: Qn, preset, en, reset
  D_Flip_Flop d_ff_3 (.clk(clock_1_out), .D(d_ff_2_q), .Q(d_ff_3_q));  // open: Qn, preset, en, reset
  D_Flip_Flop d_ff_4 (.clk(clock_1_out), .D(d_ff_3_q), .Q(out_2));  // open: Qn, preset, en, reset

  // Notes on the sheet:
  //   SISO
endmodule

module SIPO (
  input  in_1,
  output SIPO,
  output out_3,
  output out_4,
  output out_5
);

  wire clock_1_out;

  Clock clock_1 (.out(clock_1_out));
  D_Flip_Flop d_ff_1 (.clk(clock_1_out), .D(in_1), .Q(SIPO));  // open: Qn, preset, en, reset
  D_Flip_Flop d_ff_2 (.clk(clock_1_out), .D(SIPO), .Q(out_3));  // open: Qn, preset, en, reset
  D_Flip_Flop d_ff_3 (.clk(clock_1_out), .D(out_3), .Q(out_4));  // open: Qn, preset, en, reset
  D_Flip_Flop d_ff_4 (.clk(clock_1_out), .D(out_4), .Q(out_5));  // open: Qn, preset, en, reset
endmodule

module PISO (
  input  in_1,
  input  in_2,
  input  in_3,
  input  in_4,
  input  in_5,
  output out_6
);

  wire clock_1_out, d_ff_1_q, d_ff_2_q, d_ff_3_q, multiplexer_1_out, multiplexer_2_out, multiplexer_3_out,
       multiplexer_4_out;

  Clock clock_1 (.out(clock_1_out));
  Multiplexer multiplexer_1 (.in0(in_1), .in1(1'b0), .out(multiplexer_1_out), .sel(in_5));  // open: en
  D_Flip_Flop d_ff_1 (.clk(clock_1_out), .D(multiplexer_1_out), .Q(d_ff_1_q));  // open: Qn, preset, en, reset
  D_Flip_Flop d_ff_2 (.clk(clock_1_out), .D(multiplexer_2_out), .Q(d_ff_2_q));  // open: Qn, preset, en, reset
  Multiplexer multiplexer_2 (.in0(in_2), .in1(d_ff_1_q), .out(multiplexer_2_out), .sel(in_5));  // open: en
  Multiplexer multiplexer_3 (.in0(in_3), .in1(d_ff_2_q), .out(multiplexer_3_out), .sel(in_5));  // open: en
  D_Flip_Flop d_ff_3 (.clk(clock_1_out), .D(multiplexer_3_out), .Q(d_ff_3_q));  // open: Qn, preset, en, reset
  Multiplexer multiplexer_4 (.in0(in_4), .in1(d_ff_3_q), .out(multiplexer_4_out), .sel(in_5));  // open: en
  D_Flip_Flop d_ff_4 (.clk(clock_1_out), .D(multiplexer_4_out), .Q(out_6));  // open: Qn, preset, en, reset

  // Notes on the sheet:
  //   PISO
endmodule

module PIPO (
  input  in_1,
  input  in_2,
  input  in_3,
  input  in_4,
  output out_5,
  output out_6,
  output out_7,
  output out_8
);

  wire clock_1_out;

  Clock clock_1 (.out(clock_1_out));
  D_Flip_Flop d_ff_1 (.clk(clock_1_out), .D(in_1), .Q(out_5));  // open: Qn, preset, en, reset
  D_Flip_Flop d_ff_2 (.clk(clock_1_out), .D(in_2), .Q(out_6));  // open: Qn, preset, en, reset
  D_Flip_Flop d_ff_3 (.clk(clock_1_out), .D(in_3), .Q(out_7));  // open: Qn, preset, en, reset
  D_Flip_Flop d_ff_4 (.clk(clock_1_out), .D(in_4), .Q(out_8));  // open: Qn, preset, en, reset

  // Notes on the sheet:
  //   PIPO
endmodule

module _8_BIT_PIPO (
  input  in_1,
  input  in_2,
  input  in_3,
  input  in_4,
  input  in_5,
  input  in_6,
  input  in_7,
  input  in_8,
  output out_9,
  output out_10,
  output out_11,
  output out_12,
  output out_13,
  output out_14,
  output out_15,
  output out_16
);

  wire clock_1_out;

  Clock clock_1 (.out(clock_1_out));
  D_Flip_Flop d_ff_1 (.clk(clock_1_out), .D(in_1), .Q(out_9));  // open: Qn, preset, en, reset
  D_Flip_Flop d_ff_2 (.clk(clock_1_out), .D(in_2), .Q(out_10));  // open: Qn, preset, en, reset
  D_Flip_Flop d_ff_3 (.clk(clock_1_out), .D(in_3), .Q(out_11));  // open: Qn, preset, en, reset
  D_Flip_Flop d_ff_4 (.clk(clock_1_out), .D(in_4), .Q(out_12));  // open: Qn, preset, en, reset
  D_Flip_Flop d_ff_5 (.clk(clock_1_out), .D(in_5), .Q(out_13));  // open: Qn, preset, en, reset
  D_Flip_Flop d_ff_6 (.clk(clock_1_out), .D(in_6), .Q(out_14));  // open: Qn, preset, en, reset
  D_Flip_Flop d_ff_7 (.clk(clock_1_out), .D(in_7), .Q(out_15));  // open: Qn, preset, en, reset
  D_Flip_Flop d_ff_8 (.clk(clock_1_out), .D(in_8), .Q(out_16));  // open: Qn, preset, en, reset

  // Notes on the sheet:
  //   8 BIT PIPO
endmodule

module Circular_shift_register (
  input  in_1,
  input  in_2,
  input  in_3,
  input  in_4,
  input  in_5,
  output out_6,
  output out_7,
  output out_8,
  output out_9
);

  wire clock_1_out, multiplexer_1_out, multiplexer_2_out, multiplexer_3_out, multiplexer_4_out;

  Clock clock_1 (.out(clock_1_out));
  Multiplexer multiplexer_1 (.in0(in_1), .in1(out_9), .out(multiplexer_1_out), .sel(in_5));  // open: en
  D_Flip_Flop d_ff_1 (.clk(clock_1_out), .D(multiplexer_1_out), .Q(out_6));  // open: Qn, preset, en, reset
  D_Flip_Flop d_ff_2 (.clk(clock_1_out), .D(multiplexer_2_out), .Q(out_7));  // open: Qn, preset, en, reset
  Multiplexer multiplexer_2 (.in0(in_2), .in1(out_6), .out(multiplexer_2_out), .sel(in_5));  // open: en
  Multiplexer multiplexer_3 (.in0(in_3), .in1(out_7), .out(multiplexer_3_out), .sel(in_5));  // open: en
  D_Flip_Flop d_ff_3 (.clk(clock_1_out), .D(multiplexer_3_out), .Q(out_8));  // open: Qn, preset, en, reset
  Multiplexer multiplexer_4 (.in0(in_4), .in1(out_8), .out(multiplexer_4_out), .sel(in_5));  // open: en
  D_Flip_Flop d_ff_4 (.clk(clock_1_out), .D(multiplexer_4_out), .Q(out_9));  // open: Qn, preset, en, reset

  // Notes on the sheet:
  //   Circular Shift Register
endmodule

module Ring_counter (
  input  in_1,
  output out_2,
  output out_3,
  output out_4,
  output out_5
);

  wire clock_1_out;

  Clock clock_1 (.out(clock_1_out));
  D_Flip_Flop d_ff_1 (.clk(clock_1_out), .D(out_5), .Q(out_2), .preset(in_1));  // open: Qn, en, reset
  D_Flip_Flop d_ff_2 (.clk(clock_1_out), .D(out_2), .Q(out_3), .reset(in_1));  // open: Qn, preset, en
  D_Flip_Flop d_ff_3 (.clk(clock_1_out), .D(out_3), .Q(out_4), .reset(in_1));  // open: Qn, preset, en
  D_Flip_Flop d_ff_4 (.clk(clock_1_out), .D(out_4), .Q(out_5), .reset(in_1));  // open: Qn, preset, en

  // Notes on the sheet:
  //   Ring Counter
endmodule

module _5_Bit_Ring_counter (
  input  in_1,
  output out_2,
  output out_3,
  output out_4,
  output out_5,
  output out_6
);

  wire clock_1_out;

  Clock clock_1 (.out(clock_1_out));
  D_Flip_Flop d_ff_1 (.clk(clock_1_out), .D(out_6), .Q(out_2), .preset(in_1));  // open: Qn, en, reset
  D_Flip_Flop d_ff_2 (.clk(clock_1_out), .D(out_2), .Q(out_3), .reset(in_1));  // open: Qn, preset, en
  D_Flip_Flop d_ff_3 (.clk(clock_1_out), .D(out_3), .Q(out_4), .reset(in_1));  // open: Qn, preset, en
  D_Flip_Flop d_ff_4 (.clk(clock_1_out), .D(out_4), .Q(out_5), .reset(in_1));  // open: Qn, preset, en
  D_Flip_Flop d_ff_5 (.clk(clock_1_out), .D(out_5), .Q(out_6), .reset(in_1));  // open: Qn, preset, en

  // Notes on the sheet:
  //   Ring Counter with 5 Bits
endmodule

module Johnson_counter (
  output out_1,
  output out_2,
  output out_3,
  output out_4
);

  wire clock_1_out, d_ff_4_qn;

  Clock clock_1 (.out(clock_1_out));
  D_Flip_Flop d_ff_1 (.clk(clock_1_out), .D(d_ff_4_qn), .Q(out_1));  // open: Qn, preset, en, reset
  D_Flip_Flop d_ff_2 (.clk(clock_1_out), .D(out_1), .Q(out_2));  // open: Qn, preset, en, reset
  D_Flip_Flop d_ff_3 (.clk(clock_1_out), .D(out_2), .Q(out_3));  // open: Qn, preset, en, reset
  D_Flip_Flop d_ff_4 (.clk(clock_1_out), .D(out_3), .Q(out_4), .Qn(d_ff_4_qn));  // open: preset, en, reset

  // Notes on the sheet:
  //   Johnson Counter
endmodule

module _5_Bit_Johnson_Counter (
  output out_1,
  output out_2,
  output out_3,
  output out_4,
  output out_5
);

  wire clock_1_out, d_ff_5_qn;

  Clock clock_1 (.out(clock_1_out));
  D_Flip_Flop d_ff_1 (.clk(clock_1_out), .D(d_ff_5_qn), .Q(out_1));  // open: Qn, preset, en, reset
  D_Flip_Flop d_ff_2 (.clk(clock_1_out), .D(out_1), .Q(out_2));  // open: Qn, preset, en, reset
  D_Flip_Flop d_ff_3 (.clk(clock_1_out), .D(out_2), .Q(out_3));  // open: Qn, preset, en, reset
  D_Flip_Flop d_ff_4 (.clk(clock_1_out), .D(out_3), .Q(out_4));  // open: Qn, preset, en, reset
  D_Flip_Flop d_ff_5 (.clk(clock_1_out), .D(out_4), .Q(out_5), .Qn(d_ff_5_qn));  // open: preset, en, reset

  // Notes on the sheet:
  //   Johnson Counter with 5 Bits
endmodule

module Circular_shift_right_left_both (
  input  in_1,
  input  in_2,
  input  in_3,
  input  in_4,
  input  Shift_Right,
  input  [1:0] Select,
  input  Shift_Left,
  output out_8,
  output out_9,
  output out_10,
  output out_11
);

  wire CLK_out, multiplexer_1_out, multiplexer_2_out, multiplexer_3_out, multiplexer_4_out;

  Clock CLK (.out(CLK_out));
  Multiplexer #(.select(2)) multiplexer_1 (
    .in0(in_1), .in1(Shift_Right), .in2(out_9), .in3(out_8), .out(multiplexer_1_out), .sel(Select));  // open: en
  D_Flip_Flop d_ff_1 (.clk(CLK_out), .D(multiplexer_1_out), .Q(out_8));  // open: Qn, preset, en, reset
  D_Flip_Flop d_ff_2 (.clk(CLK_out), .D(multiplexer_2_out), .Q(out_9));  // open: Qn, preset, en, reset
  Multiplexer #(.select(2)) multiplexer_2 (
    .in0(in_2), .in1(out_8), .in2(out_10), .in3(out_9), .out(multiplexer_2_out), .sel(Select));  // open: en
  Multiplexer #(.select(2)) multiplexer_3 (
    .in0(in_3), .in1(out_9), .in2(out_11), .in3(out_10), .out(multiplexer_3_out), .sel(Select));  // open: en
  D_Flip_Flop d_ff_3 (.clk(CLK_out), .D(multiplexer_3_out), .Q(out_10));  // open: Qn, preset, en, reset
  Multiplexer #(.select(2)) multiplexer_4 (
    .in0(in_4), .in1(out_10), .in2(Shift_Left), .in3(out_11), .out(multiplexer_4_out), .sel(Select));  // open: en
  D_Flip_Flop d_ff_4 (.clk(CLK_out), .D(multiplexer_4_out), .Q(out_11));  // open: Qn, preset, en, reset

  // Notes on the sheet:
  //   Circular Shift Register
endmodule
