// Logisim project WEEK4_DLD_ALI_IRFAN.circ as structural Verilog: 11 circuits, main circuit DIY MEALY STATE MACHINE EXAMPLE
module DIY_MEALY_STATE_MACHINE_EXAMPLE (
  input  in_1,
  output Q2,
  output Q1,
  output Q0
);

  wire and_1_out, and_2_out, and_3_out, and_4_out, and_5_out, and_6_out, and_7_out, and_8_out, and_9_out,
       clock_1_out, d_ff_1_qn, d_ff_2_qn, d_ff_3_qn, not_1_out, or_1_out, or_2_out, or_3_out;

  not not_1 (not_1_out, in_1);
  and and_1 (and_1_out, d_ff_1_qn, d_ff_2_qn, d_ff_3_qn);
  and and_2 (and_2_out, d_ff_2_qn, d_ff_1_qn, in_1);
  and and_3 (and_3_out, Q2, Q1, Q0, in_1);
  and and_4 (and_4_out, d_ff_3_qn, d_ff_1_qn, not_1_out);
  and and_5 (and_5_out, d_ff_3_qn, d_ff_2_qn, Q0, in_1);
  and and_6 (and_6_out, Q2, Q1, Q0, in_1);
  and and_7 (and_7_out, d_ff_2_qn, d_ff_1_qn, not_1_out);
  and and_8 (and_8_out, Q2, Q1, Q0, in_1);
  and and_9 (and_9_out, d_ff_3_qn, Q1, d_ff_1_qn, in_1);
  or or_1 (or_1_out, and_1_out, and_2_out, and_3_out);
  or or_2 (or_2_out, and_4_out, and_5_out, and_6_out);
  or or_3 (or_3_out, and_7_out, and_8_out, and_9_out);
  Clock clock_1 (.out(clock_1_out));
  D_Flip_Flop d_ff_1 (.clk(clock_1_out), .D(or_1_out), .Q(Q0), .Qn(d_ff_1_qn));  // open: preset, en, reset
  D_Flip_Flop d_ff_2 (.clk(clock_1_out), .D(or_2_out), .Q(Q1), .Qn(d_ff_2_qn));  // open: preset, en, reset
  D_Flip_Flop d_ff_3 (.clk(clock_1_out), .D(or_3_out), .Q(Q2), .Qn(d_ff_3_qn));  // open: preset, en, reset
endmodule

module MODULUS_10_ASYNCHOROUS (
  input  in_1,
  input  in_2,
  output out_3,
  output Q3,
  output Q2,
  output Q1,
  output Q0
);

  wire d_ff_1_qn, d_ff_2_qn, d_ff_3_qn, d_ff_4_qn;

  D_Flip_Flop d_ff_1 (.clk(in_1), .D(d_ff_1_qn), .Q(Q0), .Qn(d_ff_1_qn), .en(in_2), .reset(out_3));  // open: preset
  D_Flip_Flop d_ff_2 (
    .clk(d_ff_1_qn), .D(d_ff_2_qn), .Q(Q1), .Qn(d_ff_2_qn), .en(in_2), .reset(out_3));  // open: preset
  D_Flip_Flop d_ff_3 (
    .clk(d_ff_2_qn), .D(d_ff_3_qn), .Q(Q2), .Qn(d_ff_3_qn), .en(in_2), .reset(out_3));  // open: preset
  D_Flip_Flop d_ff_4 (
    .clk(d_ff_3_qn), .D(d_ff_4_qn), .Q(Q3), .Qn(d_ff_4_qn), .en(in_2), .reset(out_3));  // open: preset
  and and_1 (out_3, Q1, Q3);
endmodule

module MODULUS_100_CASCADE_DECADE_COUNTER_ASYNCHOROUS (
  input  in_1,
  output out_2,
  output out_3,
  output out_4,
  output out_5,
  output out_6,
  output out_7,
  output out_8,
  output out_9
);

  wire clock_1_out, modulus_10_asynchorous_1_out_3;

  Clock clock_1 (.out(clock_1_out));
  MODULUS_10_ASYNCHOROUS modulus_10_asynchorous_1 (
    .in_1(clock_1_out), .in_2(in_1), .Q3(out_5), .Q2(out_6), .Q1(out_8), .Q0(out_7),
    .out_3(modulus_10_asynchorous_1_out_3));
  MODULUS_10_ASYNCHOROUS modulus_10_asynchorous_2 (
    .in_1(modulus_10_asynchorous_1_out_3), .in_2(in_1), .Q3(out_2), .Q2(out_9), .Q1(out_3), .Q0(out_4));  // open: out_3
endmodule

module MODULUS_10_SYNCHORUS (
  input  in_1,
  input  in_2,
  output Q3,
  output Q2,
  output Q1,
  output Q0,
  output out_7
);

  wire and_1_out, and_2_out, and_3_out, and_4_out, and_5_out, and_6_out, and_7_out, and_8_out, and_9_out,
       and_10_out, and_11_out, d_ff_1_qn, d_ff_2_qn, d_ff_3_qn, d_ff_4_qn, or_1_out, or_2_out, or_3_out,
       or_4_out;

  and and_1 (and_1_out, d_ff_4_qn, d_ff_2_qn, d_ff_1_qn);
  and and_2 (and_2_out, d_ff_4_qn, Q1, d_ff_1_qn);
  and and_3 (and_3_out, d_ff_3_qn, d_ff_2_qn, d_ff_1_qn);
  and and_4 (and_4_out, d_ff_4_qn, d_ff_2_qn, Q0);
  and and_5 (and_5_out, d_ff_4_qn, Q1, d_ff_1_qn);
  and and_6 (and_6_out, d_ff_3_qn, d_ff_2_qn, Q0);
  and and_7 (and_7_out, d_ff_4_qn, Q2, d_ff_2_qn);
  and and_8 (and_8_out, d_ff_4_qn, Q2, d_ff_1_qn);
  and and_9 (and_9_out, d_ff_4_qn, d_ff_3_qn, Q1, Q0);
  and and_10 (and_10_out, Q3, d_ff_3_qn, d_ff_2_qn);
  and and_11 (and_11_out, d_ff_4_qn, Q2, Q1, Q0);
  or or_1 (or_1_out, and_10_out, and_11_out);
  or or_2 (or_2_out, and_1_out, and_2_out, and_3_out);
  or or_3 (or_3_out, and_4_out, and_5_out, and_6_out);
  or or_4 (or_4_out, and_7_out, and_8_out, and_9_out);
  D_Flip_Flop d_ff_1 (.clk(in_2), .D(or_2_out), .Q(Q0), .Qn(d_ff_1_qn), .en(in_1), .reset(out_7));  // open: preset
  D_Flip_Flop d_ff_2 (.clk(in_2), .D(or_3_out), .Q(Q1), .Qn(d_ff_2_qn), .en(in_1), .reset(out_7));  // open: preset
  D_Flip_Flop d_ff_3 (.clk(in_2), .D(or_4_out), .Q(Q2), .Qn(d_ff_3_qn), .en(in_1), .reset(out_7));  // open: preset
  D_Flip_Flop d_ff_4 (.clk(in_2), .D(or_1_out), .Q(Q3), .Qn(d_ff_4_qn), .en(in_1), .reset(out_7));  // open: preset
  and and_12 (out_7, Q3, Q1);
endmodule

module MODULUS_100_CASCADE_DECADE_COUNTER_SYNCHOROUS (
  input  EN,
  output Q3,
  output Q2,
  output Q1,
  output Q0,
  output Q3_2,
  output Q2_2,
  output Q1_2,
  output Q0_2
);

  wire CLK_out, MOD_10_out_7;

  Clock CLK (.out(CLK_out));
  MODULUS_10_SYNCHORUS MOD_10 (.Q3(Q3), .Q2(Q2), .Q1(Q1), .Q0(Q0), .in_1(EN), .in_2(CLK_out), .out_7(MOD_10_out_7));
  MODULUS_10_SYNCHORUS MOD_100 (.Q3(Q3_2), .Q2(Q2_2), .Q1(Q1_2), .Q0(Q0_2), .in_2(MOD_10_out_7));  // open: in_1, out_7
endmodule

module MOD_6 (
  input  in_1,
  input  in_2,
  output Q3,
  output Q2,
  output Q1,
  output Q0,
  output out_7
);

  wire and_1_out, and_2_out, and_3_out, and_4_out, and_5_out, and_6_out, and_7_out, and_8_out, and_9_out,
       and_10_out, and_11_out, d_ff_1_qn, d_ff_2_qn, d_ff_3_qn, d_ff_4_qn, or_1_out, or_2_out, or_3_out,
       or_4_out;

  and and_1 (and_1_out, d_ff_4_qn, d_ff_2_qn, d_ff_1_qn);
  and and_2 (and_2_out, d_ff_4_qn, Q1, d_ff_1_qn);
  and and_3 (and_3_out, d_ff_3_qn, d_ff_2_qn, d_ff_1_qn);
  and and_4 (and_4_out, d_ff_4_qn, d_ff_2_qn, Q0);
  and and_5 (and_5_out, d_ff_4_qn, Q1, d_ff_1_qn);
  and and_6 (and_6_out, d_ff_3_qn, d_ff_2_qn, Q0);
  and and_7 (and_7_out, d_ff_4_qn, Q2, d_ff_2_qn);
  and and_8 (and_8_out, d_ff_4_qn, Q2, d_ff_1_qn);
  and and_9 (and_9_out, d_ff_4_qn, d_ff_3_qn, Q1, Q0);
  and and_10 (and_10_out, Q3, d_ff_3_qn, d_ff_2_qn);
  and and_11 (and_11_out, d_ff_4_qn, Q2, Q1, Q0);
  or or_1 (or_1_out, and_10_out, and_11_out);
  or or_2 (or_2_out, and_1_out, and_2_out, and_3_out);
  or or_3 (or_3_out, and_4_out, and_5_out, and_6_out);
  or or_4 (or_4_out, and_7_out, and_8_out, and_9_out);
  D_Flip_Flop d_ff_1 (.clk(in_2), .D(or_2_out), .Q(Q0), .Qn(d_ff_1_qn), .en(in_1), .reset(out_7));  // open: preset
  D_Flip_Flop d_ff_2 (.clk(in_2), .D(or_3_out), .Q(Q1), .Qn(d_ff_2_qn), .en(in_1), .reset(out_7));  // open: preset
  D_Flip_Flop d_ff_3 (.clk(in_2), .D(or_4_out), .Q(Q2), .Qn(d_ff_3_qn), .en(in_1), .reset(out_7));  // open: preset
  D_Flip_Flop d_ff_4 (.clk(in_2), .D(or_1_out), .Q(Q3), .Qn(d_ff_4_qn), .en(in_1), .reset(out_7));  // open: preset
  and and_12 (out_7, Q2, Q1);
endmodule

module MOD_2 (
  input  in_1,
  input  in_2,
  input  in_3,
  output Q3,
  output Q2,
  output Q1,
  output Q0,
  output out_8
);

  wire and_1_out, and_2_out, and_3_out, and_4_out, and_5_out, and_6_out, and_7_out, and_8_out, and_9_out,
       and_10_out, and_11_out, d_ff_1_qn, d_ff_2_qn, d_ff_3_qn, d_ff_4_qn, or_1_out, or_2_out, or_3_out,
       or_4_out;

  and and_1 (and_1_out, d_ff_4_qn, d_ff_2_qn, d_ff_1_qn);
  and and_2 (and_2_out, d_ff_4_qn, Q1, d_ff_1_qn);
  and and_3 (and_3_out, d_ff_3_qn, d_ff_2_qn, d_ff_1_qn);
  and and_4 (and_4_out, d_ff_4_qn, d_ff_2_qn, Q0);
  and and_5 (and_5_out, d_ff_4_qn, Q1, d_ff_1_qn);
  and and_6 (and_6_out, d_ff_3_qn, d_ff_2_qn, Q0);
  and and_7 (and_7_out, d_ff_4_qn, Q2, d_ff_2_qn);
  and and_8 (and_8_out, d_ff_4_qn, Q2, d_ff_1_qn);
  and and_9 (and_9_out, d_ff_4_qn, d_ff_3_qn, Q1, Q0);
  and and_10 (and_10_out, Q3, d_ff_3_qn, d_ff_2_qn);
  and and_11 (and_11_out, d_ff_4_qn, Q2, Q1, Q0);
  or or_1 (or_1_out, and_10_out, and_11_out);
  or or_2 (or_2_out, and_1_out, and_2_out, and_3_out);
  or or_3 (or_3_out, and_4_out, and_5_out, and_6_out);
  or or_4 (or_4_out, and_7_out, and_8_out, and_9_out);
  D_Flip_Flop d_ff_1 (.clk(in_2), .D(or_2_out), .Q(Q0), .Qn(d_ff_1_qn), .en(in_1), .reset(out_8));  // open: preset
  D_Flip_Flop d_ff_2 (.clk(in_2), .D(or_3_out), .Q(Q1), .Qn(d_ff_2_qn), .en(in_1), .reset(out_8));  // open: preset
  D_Flip_Flop d_ff_3 (.clk(in_2), .D(or_4_out), .Q(Q2), .Qn(d_ff_3_qn), .en(in_1), .reset(out_8));  // open: preset
  D_Flip_Flop d_ff_4 (.clk(in_2), .D(or_1_out), .Q(Q3), .Qn(d_ff_4_qn), .en(in_1), .reset(out_8));  // open: preset
  or or_5 (out_8, Q1, in_3);
endmodule

module MOD_10_for_hours (
  input  in_1,
  input  in_2,
  input  in_3,
  output Q3,
  output Q2,
  output Q1,
  output Q0,
  output out_8
);

  wire and_1_out, and_2_out, and_3_out, and_4_out, and_5_out, and_6_out, and_7_out, and_8_out, and_9_out,
       and_10_out, and_11_out, and_12_out, d_ff_1_qn, d_ff_2_qn, d_ff_3_qn, d_ff_4_qn, or_1_out, or_2_out,
       or_3_out, or_4_out;

  and and_1 (and_1_out, d_ff_4_qn, d_ff_2_qn, d_ff_1_qn);
  and and_2 (and_2_out, d_ff_4_qn, Q1, d_ff_1_qn);
  and and_3 (and_3_out, d_ff_3_qn, d_ff_2_qn, d_ff_1_qn);
  and and_4 (and_4_out, d_ff_4_qn, d_ff_2_qn, Q0);
  and and_5 (and_5_out, d_ff_4_qn, Q1, d_ff_1_qn);
  and and_6 (and_6_out, d_ff_3_qn, d_ff_2_qn, Q0);
  and and_7 (and_7_out, d_ff_4_qn, Q2, d_ff_2_qn);
  and and_8 (and_8_out, d_ff_4_qn, Q2, d_ff_1_qn);
  and and_9 (and_9_out, d_ff_4_qn, d_ff_3_qn, Q1, Q0);
  and and_10 (and_10_out, Q3, d_ff_3_qn, d_ff_2_qn);
  and and_11 (and_11_out, d_ff_4_qn, Q2, Q1, Q0);
  or or_1 (or_1_out, and_10_out, and_11_out);
  or or_2 (or_2_out, and_1_out, and_2_out, and_3_out);
  or or_3 (or_3_out, and_4_out, and_5_out, and_6_out);
  or or_4 (or_4_out, and_7_out, and_8_out, and_9_out);
  D_Flip_Flop d_ff_1 (.clk(in_2), .D(or_2_out), .Q(Q0), .Qn(d_ff_1_qn), .en(in_1), .reset(out_8));  // open: preset
  D_Flip_Flop d_ff_2 (.clk(in_2), .D(or_3_out), .Q(Q1), .Qn(d_ff_2_qn), .en(in_1), .reset(out_8));  // open: preset
  D_Flip_Flop d_ff_3 (.clk(in_2), .D(or_4_out), .Q(Q2), .Qn(d_ff_3_qn), .en(in_1), .reset(out_8));  // open: preset
  D_Flip_Flop d_ff_4 (.clk(in_2), .D(or_1_out), .Q(Q3), .Qn(d_ff_4_qn), .en(in_1), .reset(out_8));  // open: preset
  and and_12 (and_12_out, Q3, Q1);
  or or_5 (out_8, and_12_out, in_3);
endmodule

module DIGITAL_CLOCK (
  input  in_1,
  input  in_2,
  input  in_3
);

  wire and_1_out, bcd_to_7_seg_1_a, bcd_to_7_seg_1_b, bcd_to_7_seg_1_c, bcd_to_7_seg_1_d, bcd_to_7_seg_1_e,
       bcd_to_7_seg_1_f, bcd_to_7_seg_1_g, bcd_to_7_seg_2_a, bcd_to_7_seg_2_b, bcd_to_7_seg_2_c,
       bcd_to_7_seg_2_d, bcd_to_7_seg_2_e, bcd_to_7_seg_2_f, bcd_to_7_seg_2_g, bcd_to_7_seg_3_a,
       bcd_to_7_seg_3_b, bcd_to_7_seg_3_c, bcd_to_7_seg_3_d, bcd_to_7_seg_3_e, bcd_to_7_seg_3_f,
       bcd_to_7_seg_3_g, bcd_to_7_seg_4_a, bcd_to_7_seg_4_b, bcd_to_7_seg_4_c, bcd_to_7_seg_4_d,
       bcd_to_7_seg_4_e, bcd_to_7_seg_4_f, bcd_to_7_seg_4_g, bcd_to_7_seg_5_a, bcd_to_7_seg_5_b,
       bcd_to_7_seg_5_c, bcd_to_7_seg_5_d, bcd_to_7_seg_5_e, bcd_to_7_seg_5_f, bcd_to_7_seg_5_g,
       bcd_to_7_seg_6_a, bcd_to_7_seg_6_b, bcd_to_7_seg_6_c, bcd_to_7_seg_6_d, bcd_to_7_seg_6_e,
       bcd_to_7_seg_6_f, bcd_to_7_seg_6_g, clock_1_out, MOD_2_q0, MOD_2_q1, MOD_2_q2, MOD_2_q3,
       MOD_6_2_out_7, MOD_6_2_q0, MOD_6_2_q1, MOD_6_2_q2, MOD_6_2_q3, MOD_6_out_7, MOD_6_q0, MOD_6_q1,
       MOD_6_q2, MOD_6_q3, MOD_10_2_out_7, MOD_10_2_q0, MOD_10_2_q1, MOD_10_2_q2, MOD_10_2_q3,
       MOD_10_3_out_7, MOD_10_3_q0, MOD_10_3_q1, MOD_10_3_q2, MOD_10_3_q3, MOD_10_out_8, MOD_10_q0,
       MOD_10_q1, MOD_10_q2, MOD_10_q3;

  MOD_10_for_hours MOD_10 (
    .in_3(and_1_out), .in_1(in_1), .in_2(MOD_6_out_7), .Q3(MOD_10_q3), .Q2(MOD_10_q2), .Q1(MOD_10_q1),
    .Q0(MOD_10_q0), .out_8(MOD_10_out_8));
  BCD_to_7_Seg bcd_to_7_seg_1 (
    .W(MOD_10_q3), .X(MOD_10_q2), .Y(MOD_10_q1), .Z(MOD_10_q0), .a(bcd_to_7_seg_1_a), .b(bcd_to_7_seg_1_b),
    .c(bcd_to_7_seg_1_c), .d(bcd_to_7_seg_1_d), .e(bcd_to_7_seg_1_e), .f(bcd_to_7_seg_1_f),
    .g(bcd_to_7_seg_1_g));
  MOD_2 MOD_2 (
    .in_1(in_1), .in_2(MOD_10_out_8), .Q3(MOD_2_q3), .Q2(MOD_2_q2), .Q1(MOD_2_q1), .Q0(MOD_2_q0),
    .in_3(and_1_out));  // open: out_8
  BCD_to_7_Seg bcd_to_7_seg_2 (
    .W(MOD_2_q3), .X(MOD_2_q2), .Y(MOD_2_q1), .Z(MOD_2_q0), .a(bcd_to_7_seg_2_a), .b(bcd_to_7_seg_2_b),
    .c(bcd_to_7_seg_2_c), .d(bcd_to_7_seg_2_d), .e(bcd_to_7_seg_2_e), .f(bcd_to_7_seg_2_f),
    .g(bcd_to_7_seg_2_g));
  and and_1 (and_1_out, MOD_10_q1, MOD_10_q0, MOD_2_q0);
  _7_Segment_Display u_7_segment_display_1 (
    .g(bcd_to_7_seg_2_g), .f(bcd_to_7_seg_2_f), .a(bcd_to_7_seg_2_a), .b(bcd_to_7_seg_2_b),
    .e(bcd_to_7_seg_2_e), .d(bcd_to_7_seg_2_d), .c(bcd_to_7_seg_2_c));  // open: dp
  _7_Segment_Display u_7_segment_display_2 (
    .g(bcd_to_7_seg_1_g), .f(bcd_to_7_seg_1_f), .a(bcd_to_7_seg_1_a), .b(bcd_to_7_seg_1_b),
    .e(bcd_to_7_seg_1_e), .d(bcd_to_7_seg_1_d), .c(bcd_to_7_seg_1_c));  // open: dp
  MODULUS_10_SYNCHORUS MOD_10_2 (
    .Q3(MOD_10_2_q3), .Q2(MOD_10_2_q2), .Q1(MOD_10_2_q1), .Q0(MOD_10_2_q0), .in_1(in_2),
    .in_2(MOD_6_2_out_7), .out_7(MOD_10_2_out_7));
  BCD_to_7_Seg bcd_to_7_seg_3 (
    .W(MOD_10_2_q3), .X(MOD_10_2_q2), .Y(MOD_10_2_q1), .Z(MOD_10_2_q0), .a(bcd_to_7_seg_3_a),
    .b(bcd_to_7_seg_3_b), .c(bcd_to_7_seg_3_c), .d(bcd_to_7_seg_3_d), .e(bcd_to_7_seg_3_e),
    .f(bcd_to_7_seg_3_f), .g(bcd_to_7_seg_3_g));
  BCD_to_7_Seg bcd_to_7_seg_4 (
    .W(MOD_6_q3), .X(MOD_6_q2), .Y(MOD_6_q1), .Z(MOD_6_q0), .a(bcd_to_7_seg_4_a), .b(bcd_to_7_seg_4_b),
    .c(bcd_to_7_seg_4_c), .d(bcd_to_7_seg_4_d), .e(bcd_to_7_seg_4_e), .f(bcd_to_7_seg_4_f),
    .g(bcd_to_7_seg_4_g));
  MOD_6 MOD_6 (
    .in_1(in_2), .in_2(MOD_10_2_out_7), .Q3(MOD_6_q3), .Q2(MOD_6_q2), .Q1(MOD_6_q1), .Q0(MOD_6_q0),
    .out_7(MOD_6_out_7));
  _7_Segment_Display u_7_segment_display_3 (
    .g(bcd_to_7_seg_4_g), .f(bcd_to_7_seg_4_f), .a(bcd_to_7_seg_4_a), .b(bcd_to_7_seg_4_b),
    .e(bcd_to_7_seg_4_e), .d(bcd_to_7_seg_4_d), .c(bcd_to_7_seg_4_c));  // open: dp
  _7_Segment_Display u_7_segment_display_4 (
    .g(bcd_to_7_seg_3_g), .f(bcd_to_7_seg_3_f), .a(bcd_to_7_seg_3_a), .b(bcd_to_7_seg_3_b),
    .e(bcd_to_7_seg_3_e), .d(bcd_to_7_seg_3_d), .c(bcd_to_7_seg_3_c));  // open: dp
  Clock clock_1 (.out(clock_1_out));
  MODULUS_10_SYNCHORUS MOD_10_3 (
    .Q3(MOD_10_3_q3), .Q2(MOD_10_3_q2), .Q1(MOD_10_3_q1), .Q0(MOD_10_3_q0), .in_1(in_3), .in_2(clock_1_out),
    .out_7(MOD_10_3_out_7));
  MOD_6 MOD_6_2 (
    .in_1(in_3), .in_2(MOD_10_3_out_7), .Q3(MOD_6_2_q3), .Q2(MOD_6_2_q2), .Q1(MOD_6_2_q1), .Q0(MOD_6_2_q0),
    .out_7(MOD_6_2_out_7));
  BCD_to_7_Seg bcd_to_7_seg_5 (
    .W(MOD_10_3_q3), .X(MOD_10_3_q2), .Y(MOD_10_3_q1), .Z(MOD_10_3_q0), .a(bcd_to_7_seg_5_a),
    .b(bcd_to_7_seg_5_b), .c(bcd_to_7_seg_5_c), .d(bcd_to_7_seg_5_d), .e(bcd_to_7_seg_5_e),
    .f(bcd_to_7_seg_5_f), .g(bcd_to_7_seg_5_g));
  BCD_to_7_Seg bcd_to_7_seg_6 (
    .W(MOD_6_2_q3), .X(MOD_6_2_q2), .Y(MOD_6_2_q1), .Z(MOD_6_2_q0), .a(bcd_to_7_seg_6_a),
    .b(bcd_to_7_seg_6_b), .c(bcd_to_7_seg_6_c), .d(bcd_to_7_seg_6_d), .e(bcd_to_7_seg_6_e),
    .f(bcd_to_7_seg_6_f), .g(bcd_to_7_seg_6_g));
  _7_Segment_Display u_7_segment_display_5 (
    .g(bcd_to_7_seg_5_g), .f(bcd_to_7_seg_5_f), .a(bcd_to_7_seg_5_a), .b(bcd_to_7_seg_5_b),
    .e(bcd_to_7_seg_5_e), .d(bcd_to_7_seg_5_d), .c(bcd_to_7_seg_5_c));  // open: dp
  _7_Segment_Display u_7_segment_display_6 (
    .g(bcd_to_7_seg_6_g), .f(bcd_to_7_seg_6_f), .a(bcd_to_7_seg_6_a), .b(bcd_to_7_seg_6_b),
    .e(bcd_to_7_seg_6_e), .d(bcd_to_7_seg_6_d), .c(bcd_to_7_seg_6_c));  // open: dp

  // Notes on the sheet:
  //   HOURS
  //   MINUTES
  //   DIGITAL CLOCK
  //   SECONDS
endmodule

module _3_bit_active_high_decoding_counter_of_count_2_and_count_7 (
  input  in_1,
  output out_2,
  output out_3
);

  wire and_2_out, clock_1_out, j_k_ff_1_q, j_k_ff_1_qn, j_k_ff_2_q, j_k_ff_3_q, j_k_ff_3_qn;

  Clock clock_1 (.out(clock_1_out));
  J_K_Flip_Flop j_k_ff_1 (
    .J(in_1), .clk(clock_1_out), .K(in_1), .Q(j_k_ff_1_q), .Qn(j_k_ff_1_qn));  // open: preset, en, reset
  J_K_Flip_Flop j_k_ff_2 (
    .J(j_k_ff_1_q), .clk(clock_1_out), .K(j_k_ff_1_q), .Q(j_k_ff_2_q));  // open: Qn, preset, en, reset
  and and_1 (out_3, j_k_ff_1_qn, j_k_ff_2_q, j_k_ff_3_qn);
  and and_2 (and_2_out, j_k_ff_1_q, j_k_ff_2_q);
  J_K_Flip_Flop j_k_ff_3 (
    .J(and_2_out), .clk(clock_1_out), .K(and_2_out), .Q(j_k_ff_3_q), .Qn(j_k_ff_3_qn));  // open: preset, en, reset
  and and_3 (out_2, j_k_ff_2_q, j_k_ff_1_q, j_k_ff_3_q);
endmodule

module BCD_to_7_Seg (
  input  W,
  input  X,
  input  Y,
  input  Z,
  output a,
  output b,
  output c,
  output d,
  output e,
  output f,
  output g
);

  wire and_1_out, and_2_out, and_3_out, and_4_out, and_5_out, and_6_out, and_7_out, and_8_out, and_9_out,
       and_10_out, and_11_out, and_12_out, and_13_out, and_14_out, and_15_out, and_16_out, not_1_out,
       not_2_out, not_3_out, not_4_out, not_5_out, not_6_out, not_7_out, not_8_out, not_9_out, not_10_out,
       not_11_out, not_12_out, not_13_out, not_14_out, not_15_out, not_16_out, not_17_out, not_18_out,
       not_19_out, not_20_out, not_21_out;

  not not_1 (not_1_out, X);
  and and_1 (and_1_out, not_1_out, not_2_out);
  not not_2 (not_2_out, Z);
  and and_2 (and_2_out, X, Z);
  not not_3 (not_3_out, X);
  not not_4 (not_4_out, Y);
  and and_3 (and_3_out, not_4_out, not_5_out);
  not not_5 (not_5_out, Z);
  and and_4 (and_4_out, Y, Z);
  not not_6 (not_6_out, Y);
  or or_1 (c, not_6_out, Z, X);
  not not_7 (not_7_out, X);
  and and_5 (and_5_out, not_7_out, not_8_out);
  not not_8 (not_8_out, Z);
  not not_9 (not_9_out, X);
  and and_6 (and_6_out, not_9_out, Y);
  and and_7 (and_7_out, Y, not_10_out);
  not not_10 (not_10_out, Z);
  not not_11 (not_11_out, Y);
  and and_8 (and_8_out, X, not_11_out, Z);
  not not_12 (not_12_out, X);
  and and_9 (and_9_out, not_12_out, not_13_out);
  not not_13 (not_13_out, Z);
  and and_10 (and_10_out, Y, not_14_out);
  not not_14 (not_14_out, Z);
  not not_15 (not_15_out, Y);
  and and_11 (and_11_out, not_15_out, not_16_out);
  not not_16 (not_16_out, Z);
  and and_12 (and_12_out, X, not_17_out);
  not not_17 (not_17_out, Y);
  and and_13 (and_13_out, X, not_18_out);
  not not_18 (not_18_out, Z);
  not not_19 (not_19_out, X);
  and and_14 (and_14_out, not_19_out, Y);
  and and_15 (and_15_out, X, not_20_out);
  not not_20 (not_20_out, Y);
  and and_16 (and_16_out, X, not_21_out);
  not not_21 (not_21_out, Z);
  or or_2 (a, and_1_out, Y, and_2_out, W);
  or or_3 (b, not_3_out, and_3_out, and_4_out);
  or or_4 (d, and_5_out, and_6_out, and_7_out, and_8_out, W);
  or or_5 (e, and_9_out, and_10_out);
  or or_6 (f, and_11_out, and_12_out, and_13_out, W);
  or or_7 (g, and_14_out, and_15_out, and_16_out, W);
  _7_Segment_Display u_7_segment_display_1 (.g(g), .f(f), .a(a), .b(b), .e(e), .d(d), .c(c));  // open: dp
endmodule
